// Logisim project NC16.circ as structural Verilog: 1 circuit, main circuit main
module main (
  input  [15:0] in_1
);

  wire clock_1_out, decoder_1_out0, decoder_1_out1, decoder_1_out2, decoder_1_out3, decoder_1_out4,
       decoder_1_out5, decoder_1_out6, decoder_1_out7, decoder_1_out8, dipswitch_1_sw5, not_1_out, RESET_out;
  wire [1:0] counter_1_q;
  wire [2:0] dipswitch_2_sw3, shift_register_1_p6;
  wire [3:0] dipswitch_1_sw4;
  wire [6:0] Instruction_Decorder_out;
  wire [15:0] A_q, adder_1_out, and_2_out, B_q, C_q, D_q, demultiplexer_1_out0, demultiplexer_1_out1,
       demultiplexer_2_out0, demultiplexer_2_out1, demultiplexer_2_out2, demultiplexer_2_out3,
       demultiplexer_2_out4, demultiplexer_2_out5, demultiplexer_2_out6, demultiplexer_2_out7,
       demultiplexer_3_out0, demultiplexer_3_out1, demultiplexer_3_out2, demultiplexer_3_out3,
       demultiplexer_3_out4, demultiplexer_3_out6, demultiplexer_3_out7, divider_1_out, E_q, F_q,
       Input_data_sw16, multiplexer_1_out, multiplexer_2_out, multiplexer_3_out, multiplexer_4_out,
       multiplexer_5_out, multiplexer_6_out, multiplexer_7_out, multiplexer_8_out, multiplexer_9_out,
       multiplexer_10_out, multiplexer_11_out, multiplexer_12_out, multiplexer_13_out, multiplexer_14_out,
       multiplier_1_out, not_2_out, or_1_out, Output_data_q, PC_q, ram_2_dout, shift_register_1_p4,
       shift_register_1_p5, SP_q, subtractor_1_out, xor_1_out;
  wire [16:16] and_1_out;

  DipSwitch #(.number(16)) Input_data (
    .sw1(Input_data_sw16[15]), .sw2(Input_data_sw16[14]), .sw3(Input_data_sw16[13]),
    .sw4(Input_data_sw16[12]), .sw5(Input_data_sw16[11]), .sw6(Input_data_sw16[10]),
    .sw7(Input_data_sw16[9]), .sw8(Input_data_sw16[8]), .sw9(Input_data_sw16[7]), .sw10(Input_data_sw16[6]),
    .sw11(Input_data_sw16[5]), .sw12(Input_data_sw16[4]), .sw13(Input_data_sw16[3]),
    .sw14(Input_data_sw16[2]), .sw15(Input_data_sw16[1]), .sw16(Input_data_sw16[0]));
  Clock clock_1 (.out(clock_1_out));
  Button RESET (.out(RESET_out));
  Decoder #(.select(4)) decoder_1 (
    .out0(decoder_1_out0), .out1(decoder_1_out1), .out2(decoder_1_out2), .out3(decoder_1_out3),
    .out4(decoder_1_out4), .out5(decoder_1_out5), .out6(decoder_1_out6), .out7(decoder_1_out7),
    .out8(decoder_1_out8), .sel(Instruction_Decorder_out[6:3]));  // open: out9, out10, out11, out12, out13, out14, out15, en
  LedBar #(.matrixcols(16)) ledbar_1 (
    .led0(multiplexer_12_out[15]), .led1(multiplexer_12_out[14]), .led2(multiplexer_12_out[13]),
    .led3(multiplexer_12_out[12]), .led4(multiplexer_12_out[11]), .led5(multiplexer_12_out[10]),
    .led6(multiplexer_12_out[9]), .led7(multiplexer_12_out[8]), .led8(multiplexer_12_out[7]),
    .led9(multiplexer_12_out[6]), .led10(multiplexer_12_out[5]), .led11(multiplexer_12_out[4]),
    .led12(multiplexer_12_out[3]), .led13(multiplexer_12_out[2]), .led14(multiplexer_12_out[1]),
    .led15(multiplexer_12_out[0]));
  Multiplexer #(.width(16)) multiplexer_1 (
    .in0(A_q), .in1(multiplexer_12_out), .out(multiplexer_1_out), .sel(decoder_1_out0));
  Multiplexer #(.width(16)) multiplexer_2 (
    .in0(B_q), .in1(multiplexer_12_out), .out(multiplexer_2_out), .sel(decoder_1_out1));
  Multiplexer #(.width(16)) multiplexer_3 (
    .in0(C_q), .in1(multiplexer_12_out), .out(multiplexer_3_out), .sel(decoder_1_out2));
  Multiplexer #(.width(16)) multiplexer_4 (
    .in0(D_q), .in1(multiplexer_12_out), .out(multiplexer_4_out), .sel(decoder_1_out3));
  Multiplexer #(.width(16)) multiplexer_5 (
    .in0(E_q), .in1(multiplexer_12_out), .out(multiplexer_5_out), .sel(decoder_1_out4));
  Multiplexer #(.width(16)) multiplexer_6 (
    .in0(F_q), .in1(multiplexer_12_out), .out(multiplexer_6_out), .sel(decoder_1_out5));
  Multiplexer #(.width(16)) multiplexer_7 (
    .in0(SP_q), .in1(multiplexer_12_out), .out(multiplexer_7_out), .sel(decoder_1_out6));
  Counter #(.max('hffff), .width(16)) PC (
    .clr(RESET_out), .load(decoder_1_out7), .clk(clock_1_out), .D(multiplexer_8_out), .Q(PC_q));  // open: up, count, carry
  Multiplexer #(.width(16)) multiplexer_8 (
    .in0(PC_q), .in1(multiplexer_12_out), .out(multiplexer_8_out), .sel(decoder_1_out7));
  Multiplexer #(.width(16)) multiplexer_9 (
    .in0(Output_data_q), .in1(multiplexer_12_out), .out(multiplexer_9_out), .sel(decoder_1_out8));
  Register #(.width(16)) A (.D(multiplexer_1_out), .en(decoder_1_out0), .clk(clock_1_out), .Q(A_q), .clr(RESET_out));
  Register #(.width(16)) B (.D(multiplexer_2_out), .en(decoder_1_out1), .clk(clock_1_out), .Q(B_q), .clr(RESET_out));
  Register #(.width(16)) C (.D(multiplexer_3_out), .en(decoder_1_out2), .clk(clock_1_out), .Q(C_q), .clr(RESET_out));
  Register #(.width(16)) D (.D(multiplexer_4_out), .en(decoder_1_out3), .clk(clock_1_out), .Q(D_q), .clr(RESET_out));
  Register #(.width(16)) E (.D(multiplexer_5_out), .en(decoder_1_out4), .clk(clock_1_out), .Q(E_q), .clr(RESET_out));
  Register #(.width(16)) F (.D(multiplexer_6_out), .en(decoder_1_out5), .clk(clock_1_out), .Q(F_q), .clr(RESET_out));
  Register #(.width(16)) SP (.D(multiplexer_7_out), .en(decoder_1_out6), .clk(clock_1_out), .Q(SP_q), .clr(RESET_out));
  Register #(.width(16)) Output_data (
    .D(multiplexer_9_out), .en(decoder_1_out8), .clk(clock_1_out), .Q(Output_data_q), .clr(RESET_out));
  RAM #(.addrWidth(16), .dataWidth(16), .enables("line")) ram_1 (.addr(in_1));  // open: we, clk, din, dout
  Multiplexer #(.select(2), .width(16)) multiplexer_10 (
    .in0(PC_q), .in1(A_q), .in2(shift_register_1_p4), .out(multiplexer_10_out),
    .sel(Instruction_Decorder_out[2:1]));  // open: in3
  RAM #(.addrWidth(16), .dataWidth(16), .enables("line")) ram_2 (
    .addr(multiplexer_10_out), .we(Instruction_Decorder_out[0]), .clk(clock_1_out), .din(B_q),
    .dout(ram_2_dout));
  LedBar #(.matrixcols(16)) ledbar_2 (
    .led0(Output_data_q[15]), .led1(Output_data_q[14]), .led2(Output_data_q[13]), .led3(Output_data_q[12]),
    .led4(Output_data_q[11]), .led5(Output_data_q[10]), .led6(Output_data_q[9]), .led7(Output_data_q[8]),
    .led8(Output_data_q[7]), .led9(Output_data_q[6]), .led10(Output_data_q[5]), .led11(Output_data_q[4]),
    .led12(Output_data_q[3]), .led13(Output_data_q[2]), .led14(Output_data_q[1]), .led15(Output_data_q[0]));
  Multiplexer #(.select(4), .width(16)) multiplexer_11 (
    .in0(A_q), .in1(B_q), .in2(C_q), .in3(D_q), .in4(E_q), .in5(F_q), .in6(SP_q), .in7(Input_data_sw16),
    .in8(ram_2_dout), .out(multiplexer_11_out), .sel(dipswitch_1_sw4));  // open: in9, in10, in11, in12, in13, in14, in15
  DipSwitch #(.number(5)) dipswitch_1 (
    .sw1(dipswitch_1_sw4[3]), .sw2(dipswitch_1_sw4[2]), .sw3(dipswitch_1_sw4[1]), .sw4(dipswitch_1_sw4[0]),
    .sw5(dipswitch_1_sw5));
  // Shift_Register #(.length(2), .width(16)) shift_register_1: pin names not known; wires that end beside it: RESET_out, clock_1_out, ram_2_dout, shift_register_1_p4, shift_register_1_p5, shift_register_1_p6, shift_register_1_p6
  Counter #(.max('h3), .width(2)) counter_1 (
    .clr(RESET_out), .load(and_1_out[16]), .clk(clock_1_out), .D(2'b01), .Q(counter_1_q));  // open: up, count, carry
  Multiplexer #(.width(16)) multiplexer_12 (
    .in0(demultiplexer_1_out0), .in1(multiplexer_14_out), .out(multiplexer_12_out), .sel(dipswitch_1_sw5));
  Demultiplexer #(.width(16)) demultiplexer_1 (
    .out0(demultiplexer_1_out0), .out1(demultiplexer_1_out1), .in(multiplexer_11_out), .sel(dipswitch_1_sw5));
  Demultiplexer #(.select(3), .width(16)) demultiplexer_2 (
    .out0(demultiplexer_2_out0), .out1(demultiplexer_2_out1), .out2(demultiplexer_2_out2),
    .out3(demultiplexer_2_out3), .out4(demultiplexer_2_out4), .out5(demultiplexer_2_out5),
    .out6(demultiplexer_2_out6), .out7(demultiplexer_2_out7), .in(demultiplexer_1_out1), .sel(dipswitch_2_sw3));
  DipSwitch #(.number(3)) dipswitch_2 (.sw1(dipswitch_2_sw3[2]), .sw2(dipswitch_2_sw3[1]), .sw3(dipswitch_2_sw3[0]));
  DipSwitch #(.number(3)) dipswitch_3 (
    .sw1(shift_register_1_p6[2]), .sw2(shift_register_1_p6[1]), .sw3(shift_register_1_p6[0]));
  Multiplexer #(.select(3), .width(16)) multiplexer_13 (
    .in0(A_q), .in1(B_q), .in2(C_q), .in3(D_q), .in4(E_q), .in5(F_q), .in6(SP_q), .in7(shift_register_1_p4),
    .out(multiplexer_13_out), .sel(shift_register_1_p6));
  not not_1 (not_1_out, counter_1_q[0]);
  Demultiplexer #(.select(3), .width(16)) demultiplexer_3 (
    .out0(demultiplexer_3_out0), .out1(demultiplexer_3_out1), .out2(demultiplexer_3_out2),
    .out3(demultiplexer_3_out3), .out4(demultiplexer_3_out4), .out6(demultiplexer_3_out6),
    .out7(demultiplexer_3_out7), .in(multiplexer_13_out), .sel(dipswitch_2_sw3));  // open: out5
  and and_1 (and_1_out[16], not_1_out, counter_1_q[1]);
  LED led_1 (.in(and_1_out[16]));
  PLA #(.in_width(17), .out_width(7), .\table ("11111111111111111 0000010\n11101011100000000 1111011\nxxxxxxxxxxxxxxxxx 1111000")) Instruction_Decorder (
    .in({and_1_out[16], shift_register_1_p5}), .out(Instruction_Decorder_out));
  Adder #(.width(16)) adder_1 (
    .a(demultiplexer_2_out0), .b(demultiplexer_3_out0), .out(adder_1_out));  // open: cin, cout
  Subtractor #(.width(16)) subtractor_1 (
    .a(demultiplexer_2_out1), .b(demultiplexer_3_out1), .out(subtractor_1_out));  // open: bin, bout
  Multiplier #(.width(16)) multiplier_1 (
    .a(demultiplexer_2_out2), .b(demultiplexer_3_out2), .out(multiplier_1_out));  // open: cin, cout
  assign and_2_out = demultiplexer_2_out3 & demultiplexer_3_out3;  // AND_Gate and_2, 16 bits wide
  assign or_1_out = demultiplexer_2_out4 | demultiplexer_3_out4;  // OR_Gate or_1, 16 bits wide
  assign not_2_out = ~demultiplexer_2_out5;  // NOT_Gate not_2, 16 bits wide
  assign xor_1_out = demultiplexer_2_out6 ^ demultiplexer_3_out6;  // XOR_Gate xor_1, 16 bits wide
  Divider #(.width(16)) divider_1 (
    .a(demultiplexer_3_out7), .b(demultiplexer_2_out7), .out(divider_1_out));  // open: upper, rem
  Multiplexer #(.select(3), .width(16)) multiplexer_14 (
    .in0(adder_1_out), .in1(subtractor_1_out), .in2(multiplier_1_out), .in3(and_2_out), .in4(or_1_out),
    .in5(not_2_out), .in6(xor_1_out), .in7(divider_1_out), .out(multiplexer_14_out), .sel(dipswitch_2_sw3));

  // Notes on the sheet:
  //   REGISTERS
endmodule
